# Fritzing sketch 06_alarm (saved by Fritzing 0.9.3b)
breadboards: 1

parts:
  R1 = Resistor [tolerance=±5% resistance=330 package=THT]
  LED1 = LED - 3mm [color="Red (633nm)" package="3 mm [THT]"]
  R2 = Resistor [tolerance=±5% resistance=750 package=THT]
  M1 = DOIT Esp32 DevKit v1 (30 pins long, 11 pins width) [part_number=ESP32S-PIN30]
  R3 = Resistor [tolerance=±5% resistance=4.7k package=THT]
  J1 = Piezo Speaker
  S2 = Reed switch [package=THT]

nets:
  N1: R1.Pin_0, M1.D2
  N2: R1.Pin_1, LED1.anode
  N3: LED1.cathode, M1.GND, R3.Pin_0, J1.pin1
  N4: R2.Pin_0, M1.D4
  N5: R2.Pin_1, J1.pin2
  N6: M1.D5, R3.Pin_1, S2.pin_1

custom parts:
  DOIT Esp32 DevKit v1 (30 pins long, 11 pins width): The DOIT Esp32 DevKit v1 is one of the development board created by DOIT to evaluate the ESP-WROOM-32 module. It is based on the ESP32 microcontroller that boasts Wifi, Bluetooth, Ethernet and Low Power support all in a single chip. (vanepp) made breadboard work, adjusted pin numbering and labels and reduced size of schematic and cleaned up pcb. This chip is 30pins long (2 x15) and 11 pins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
